# Fritzing sketch Temp_HUD (saved by Fritzing 0.8.3b)
circuit board: 19cm x 4.5cm

parts:
  DHT11 = Humidity and Temperature Sensor RHT03
  LED1 = LEDs [package=led10mm]
  LED2 = LEDs [package=led10mm]
  LED3 = LEDs [package=led10mm]
  LED4 = LEDs [package=led10mm]
  LED5 = LEDs [package=led10mm]
  LED6 = LEDs [package=led10mm]
  LED7 = LEDs [package=led10mm]
  LED8 = LEDs [package=led10mm]
  LED9 = LEDs [package=led10mm]
  LED10 = LEDs [package=led10mm]
  LED11 = LEDs [package=led10mm]
  LED12 = LEDs [package=led10mm]
  LED13 = LEDs [package=led10mm]
  LED14 = LEDs [package=led10mm]
  LED15 = LEDs [package=led10mm]
  LED16 = LEDs [package=led10mm]
  5v_Regulator = Voltage Regulator - 5V [package="TO220 [THT]"]
  ShiftReg-2 = 74HC595 [package="DIP16 [THT]"]
  R1 = Resistor [tolerance=±5% resistance=330 package=THT]
  R2 = Resistor [tolerance=±5% resistance=330 package=THT]
  R3 = Resistor [tolerance=±5% resistance=330 package=THT]
  R4 = Resistor [tolerance=±5% resistance=330 package=THT]
  R5 = Resistor [tolerance=±5% resistance=330 package=THT]
  R6 = Resistor [tolerance=±5% resistance=330 package=THT]
  R7 = Resistor [tolerance=±5% resistance=330 package=THT]
  R8 = Resistor [tolerance=±5% resistance=330 package=THT]
  R9 = Resistor [tolerance=±5% resistance=330 package=THT]
  R10 = Resistor [tolerance=±5% resistance=330 package=THT]
  R11 = Resistor [tolerance=±5% resistance=330 package=THT]
  R12 = Resistor [tolerance=±5% resistance=330 package=THT]
  R13 = Resistor [tolerance=±5% resistance=330 package=THT]
  R14 = Resistor [tolerance=±5% resistance=330 package=THT]
  R15 = Resistor [tolerance=±5% resistance=330 package=THT]
  R16 = Resistor [tolerance=±5% resistance=330 package=THT]
  Arduini_Pro_Mini = Arduino Pro Mini v13
  ShiftReg-1 = 74HC595 [package="DIP16 [THT]"]

nets:
  VCC: DHT11.Vcc, 5v_Regulator.output_voltage, ShiftReg-2.MR, ShiftReg-2.VCC, Arduini_Pro_Mini.VCC, ShiftReg-1.MR, ShiftReg-1.VCC
  N1: DHT11.Data-signal, Arduini_Pro_Mini.A3
  GND: DHT11.GND_2, 5v_Regulator.GND, ShiftReg-2.GND, ShiftReg-2.OE, R1.Pin_1, R2.Pin_1, R3.Pin_1, R4.Pin_1, R5.Pin_1, R6.Pin_1, R7.Pin_1, R8.Pin_1, R9.Pin_1, R10.Pin_1, R11.Pin_1, R12.Pin_1, R13.Pin_1, R14.Pin_1, R15.Pin_1, R16.Pin_1, Arduini_Pro_Mini.GND, ShiftReg-1.GND, ShiftReg-1.OE
  N2: LED1.A, ShiftReg-1.Q0
  N3: LED1.C, R1.Pin_0
  N4: LED2.A, ShiftReg-1.Q1
  N5: LED2.C, R2.Pin_0
  N6: LED3.A, ShiftReg-1.Q2
  N7: LED3.C, R3.Pin_0
  N8: LED4.A, ShiftReg-1.Q3
  N9: LED4.C, R4.Pin_0
  N10: LED5.A, ShiftReg-1.Q4
  N11: LED5.C, R5.Pin_0
  N12: LED6.A, ShiftReg-1.Q5
  N13: LED6.C, R6.Pin_0
  N14: LED7.A, ShiftReg-1.Q6
  N15: LED7.C, R7.Pin_0
  N16: LED8.A, ShiftReg-1.Q7
  N17: LED8.C, R8.Pin_0
  N18: LED9.A, ShiftReg-2.Q0
  N19: LED9.C, R9.Pin_0
  N20: LED10.A, ShiftReg-2.Q1
  N21: LED10.C, R10.Pin_0
  N22: LED11.A, ShiftReg-2.Q2
  N23: LED11.C, R11.Pin_0
  N24: LED12.A, ShiftReg-2.Q3
  N25: LED12.C, R12.Pin_0
  N26: LED13.A, ShiftReg-2.Q4
  N27: LED13.C, R13.Pin_0
  N28: LED14.A, ShiftReg-2.Q5
  N29: LED14.C, R14.Pin_0
  N30: LED15.A, ShiftReg-2.Q6
  N31: LED15.C, R15.Pin_0
  N32: LED16.A, ShiftReg-2.Q7
  N33: LED16.C, R16.Pin_0
  N34: ShiftReg-2.Q7', ShiftReg-1.DS
  N35: ShiftReg-2.SH_CP, Arduini_Pro_Mini.D10_PWM/SS, ShiftReg-1.SH_CP
  N36: ShiftReg-2.ST_CP, Arduini_Pro_Mini.D9_PWM, ShiftReg-1.ST_CP
  N37: ShiftReg-2.DS, Arduini_Pro_Mini.D8
